// Logisim project LOGIC GATES.circ as structural Verilog: 1 circuit, main circuit main
module main (
  input  in_1,
  input  in_2,
  input  in_3,
  input  in_4,
  input  in_5,
  input  in_6,
  input  in_7,
  input  in_8,
  input  in_9,
  input  in_10,
  input  in_11,
  input  in_12,
  input  in_13,
  output out_14,
  output out_15,
  output out_16,
  output out_17,
  output out_18,
  output out_19,
  output out_20
);

  wire and_2_out, and_3_out, and_4_out, and_5_out, and_6_out, not_4_out, not_5_out, not_6_out, not_7_out,
       or_2_out;

  not not_1 (out_15, in_3);
  and and_1 (out_17, in_6, in_9, in_9);
  or or_1 (out_20, in_11, in_12, in_12);
  and and_2 (and_2_out, in_2, in_2, in_4);
  or or_2 (or_2_out, in_7, in_8);
  not not_2 (out_14, and_2_out);
  not not_3 (out_18, or_2_out);
  not not_4 (not_4_out, in_1);
  not not_5 (not_5_out, in_5);
  not not_6 (not_6_out, in_10);
  not not_7 (not_7_out, in_13);
  and and_3 (and_3_out, in_1, in_1, not_5_out);
  and and_4 (and_4_out, not_4_out, in_5);
  and and_5 (and_5_out, in_10, in_13);
  and and_6 (and_6_out, not_6_out, not_7_out, not_7_out);
  or or_3 (out_16, and_3_out, and_4_out);
  or or_4 (out_19, and_5_out, and_6_out);

  // Notes on the sheet:
  //   NOT GATE
  //   AND GATE
  //   OR GATE
  //   BASIC LOGIC GATES
  //   NAND GATE =AND GATE + NOT GATE
  //   NOR GATE = OR GATE + NOT GATE
  //   UNIVERSAL LOGIC GATES
  //   XNOR GATE
  //   XOR GATE
  //   SPECIAL PURPOSE GATES
endmodule
